// Logisim project regis.circ as structural Verilog: 1 circuit, main circuit main
module main (
);

  wire clock_1_out, clock_2_out, clock_3_out, d_ff_1_q, d_ff_2_q, d_ff_3_q, d_ff_4_q, d_ff_5_q, d_ff_6_q,
       d_ff_7_q, d_ff_8_q, d_ff_9_q, d_ff_10_q, d_ff_11_q, d_ff_12_q, d_ff_13_q, d_ff_14_q, d_ff_15_q,
       d_ff_16_q, multiplexer_1_out, nand_1_out, nand_2_out, nand_3_out, nand_4_out, not_1_out;
  wire [7:0] divider_1_out, divider_1_rem, divider_2_out, divider_2_rem, divider_3_out, divider_3_rem,
       divider_4_out, divider_4_rem, divider_5_out, divider_5_rem, divider_6_out, divider_6_rem,
       divider_7_out, divider_7_rem;

  Clock clock_1 (.out(clock_1_out));
  LED led_1 (.in(d_ff_1_q));
  D_Flip_Flop d_ff_1 (.D(1'b1), .clk(clock_1_out), .Q(d_ff_1_q));  // open: Qn, preset, reset
  Clock clock_2 (.out(clock_2_out));
  LED led_2 (.in(d_ff_2_q));
  D_Flip_Flop d_ff_2 (.D(d_ff_1_q), .clk(clock_1_out), .Q(d_ff_2_q));  // open: Qn, preset, reset
  not not_1 (not_1_out, 1'b0);
  D_Flip_Flop d_ff_3 (.D(d_ff_2_q), .clk(clock_1_out), .Q(d_ff_3_q));  // open: Qn, preset, reset
  LED led_3 (.in(d_ff_3_q));
  D_Flip_Flop d_ff_4 (.D(d_ff_3_q), .clk(clock_1_out), .Q(d_ff_4_q));  // open: Qn, preset, reset
  nand nand_1 (nand_1_out, 1'b0, clock_2_out);
  nand nand_2 (nand_2_out, not_1_out, clock_2_out);
  LED led_4 (.in(d_ff_4_q));
  D_Flip_Flop d_ff_5 (.D(d_ff_4_q), .clk(clock_1_out), .Q(d_ff_5_q));  // open: Qn, preset, reset
  nand nand_3 (nand_3_out, nand_1_out, nand_4_out);
  nand nand_4 (nand_4_out, nand_3_out, nand_2_out);
  LED led_5 (.in(d_ff_5_q));
  D_Flip_Flop d_ff_6 (.D(d_ff_5_q), .clk(clock_1_out), .Q(d_ff_6_q));  // open: Qn, preset, reset
  LED led_6 (.in(d_ff_6_q));
  D_Flip_Flop d_ff_7 (.D(d_ff_6_q), .clk(clock_1_out), .Q(d_ff_7_q));  // open: Qn, preset, reset
  LED led_7 (.in(d_ff_7_q));
  LED led_8 (.in(nand_3_out));
  LED led_9 (.in(nand_4_out));
  D_Flip_Flop d_ff_8 (.D(d_ff_7_q), .clk(clock_1_out), .Q(d_ff_8_q));  // open: Qn, preset, reset
  LED led_10 (.in(d_ff_8_q));
  Divider divider_1 (.a(8'ha), .b(8'h2), .out(divider_1_out), .rem(divider_1_rem));  // open: upper
  Divider divider_2 (.a(divider_1_out), .b(8'h2), .out(divider_2_out), .rem(divider_2_rem));  // open: upper
  Divider divider_3 (.a(divider_2_out), .b(8'h2), .out(divider_3_out), .rem(divider_3_rem));  // open: upper
  Divider divider_4 (.a(divider_3_out), .b(8'h2), .out(divider_4_out), .rem(divider_4_rem));  // open: upper
  Divider divider_5 (.a(divider_4_out), .b(8'h2), .out(divider_5_out), .rem(divider_5_rem));  // open: upper
  Divider divider_6 (.a(divider_5_out), .b(8'h2), .out(divider_6_out), .rem(divider_6_rem));  // open: upper
  Divider divider_7 (.a(divider_6_out), .b(8'h2), .out(divider_7_out), .rem(divider_7_rem));  // open: upper
  Multiplexer #(.select(3)) multiplexer_1 (
    .in0(divider_1_rem[0]), .in1(divider_2_rem[0]), .in2(divider_3_rem[0]), .in3(divider_4_rem[0]),
    .in4(divider_5_rem[0]), .in5(divider_6_rem[0]), .in6(divider_7_rem[0]), .in7(divider_7_out[0]),
    .out(multiplexer_1_out), .sel(3'b111));
  Clock clock_3 (.out(clock_3_out));
  LED led_11 (.in(d_ff_9_q));
  D_Flip_Flop d_ff_9 (.D(multiplexer_1_out), .clk(clock_3_out), .Q(d_ff_9_q));  // open: Qn, preset, reset
  LED led_12 (.in(d_ff_10_q));
  D_Flip_Flop d_ff_10 (.D(d_ff_9_q), .clk(clock_3_out), .Q(d_ff_10_q));  // open: Qn, preset, reset
  D_Flip_Flop d_ff_11 (.D(d_ff_10_q), .clk(clock_3_out), .Q(d_ff_11_q));  // open: Qn, preset, reset
  LED led_13 (.in(d_ff_11_q));
  D_Flip_Flop d_ff_12 (.D(d_ff_11_q), .clk(clock_3_out), .Q(d_ff_12_q));  // open: Qn, preset, reset
  LED led_14 (.in(d_ff_12_q));
  D_Flip_Flop d_ff_13 (.D(d_ff_12_q), .clk(clock_3_out), .Q(d_ff_13_q));  // open: Qn, preset, reset
  LED led_15 (.in(d_ff_13_q));
  D_Flip_Flop d_ff_14 (.D(d_ff_13_q), .clk(clock_3_out), .Q(d_ff_14_q));  // open: Qn, preset, reset
  LED led_16 (.in(d_ff_14_q));
  D_Flip_Flop d_ff_15 (.D(d_ff_14_q), .clk(clock_3_out), .Q(d_ff_15_q));  // open: Qn, preset, reset
  LED led_17 (.in(d_ff_15_q));
  D_Flip_Flop d_ff_16 (.D(d_ff_15_q), .clk(clock_3_out), .Q(d_ff_16_q));  // open: Qn, preset, reset
  LED led_18 (.in(d_ff_16_q));
endmodule
