// Logisim project mux.circ as structural Verilog: 1 circuit, main circuit main
module main (
);

  wire multiplexer_1_out, multiplexer_2_out, multiplexer_3_out, multiplexer_4_out, multiplexer_5_out,
       multiplexer_6_out, multiplexer_7_out, multiplexer_8_out, or_1_out, or_2_out, or_3_out, undriven;
  wire [2:0] priority_encoder_1_out;

  Multiplexer #(.select(3)) multiplexer_1 (
    .in0(1'b0), .in1(1'b0), .in2(1'b0), .in3(1'b0), .in4(1'b0), .in5(1'b0), .in6(1'b1), .in7(1'b1),
    .out(multiplexer_1_out), .sel(3'b111));
  Multiplexer multiplexer_2 (.in0(1'b0), .in1(1'b0), .out(multiplexer_2_out), .sel(1'b1));
  Multiplexer multiplexer_3 (.in0(1'b0), .in1(1'b0), .out(multiplexer_3_out), .sel(1'b1));
  Multiplexer multiplexer_4 (.in0(1'b1), .in1(1'b1), .out(multiplexer_4_out), .sel(1'b1));
  Multiplexer multiplexer_5 (.in0(1'b1), .in1(1'b1), .out(multiplexer_5_out), .sel(1'b1));
  LED led_1 (.in(multiplexer_1_out));
  Multiplexer multiplexer_6 (.in0(multiplexer_2_out), .in1(multiplexer_3_out), .out(multiplexer_6_out), .sel(1'b1));
  Multiplexer multiplexer_7 (.in0(multiplexer_4_out), .in1(multiplexer_5_out), .out(multiplexer_7_out), .sel(1'b1));
  Priority_Encoder priority_encoder_1 (
    .in0(1'b0), .in1(undriven), .in2(1'b1), .in3(1'b0), .in4(1'b0), .in5(1'b0), .in6(1'b0), .in7(1'b0),
    .out(priority_encoder_1_out));  // open: en_in, gs, en_out
  // Probe on priority_encoder_1_out
  or or_1 (or_1_out, 1'b0, 1'b0, 1'b0, 1'b0);
  or or_2 (or_2_out, 1'b0, 1'b0, 1'b0, 1'b0);
  or or_3 (or_3_out, 1'b0, 1'b0, 1'b0, 1'b0);
  Multiplexer multiplexer_8 (.in0(multiplexer_6_out), .in1(multiplexer_7_out), .out(multiplexer_8_out), .sel(1'b0));
  // Probe on or_1_out
  // Probe on or_2_out
  // Probe on or_3_out
  LED led_2 (.in(multiplexer_8_out));
endmodule
