// Logisim project rippleadd.circ as structural Verilog: 1 circuit, main circuit main
module main (
);

  wire and_1_out, and_2_out, and_3_out, and_4_out, and_5_out, and_6_out, and_7_out, and_8_out, and_9_out,
       and_10_out, and_11_out, and_12_out, and_13_out, and_14_out, and_15_out, and_16_out, and_17_out,
       and_18_out, and_19_out, and_20_out, and_21_out, and_22_out, and_23_out, and_24_out, and_25_out,
       and_26_out, and_27_out, and_28_out, clock_1_out, not_1_out, not_2_out, not_3_out, not_4_out,
       not_5_out, not_6_out, not_7_out, not_8_out, not_9_out, not_10_out, not_11_out, not_12_out, or_3_out,
       or_5_out, or_7_out;
  wire [4:0] or_8_out;

  not not_1 (not_1_out, 1'b1);
  not not_2 (not_2_out, 1'b0);
  not not_3 (not_3_out, or_3_out);
  and and_1 (and_1_out, 1'b1, 1'b0, or_3_out);
  and and_2 (and_2_out, not_1_out, not_2_out, or_3_out);
  and and_3 (and_3_out, not_1_out, 1'b0, not_3_out);
  and and_4 (and_4_out, 1'b1, not_3_out);
  and and_5 (and_5_out, 1'b1, 1'b0);
  and and_6 (and_6_out, 1'b0, or_3_out);
  and and_7 (and_7_out, or_3_out, 1'b1);
  or or_1 (or_8_out[4], and_5_out, and_6_out, and_7_out);
  or or_2 (or_8_out[3], and_1_out, and_2_out, and_3_out, and_4_out);
  not not_4 (not_4_out, 1'b1);
  not not_5 (not_5_out, 1'b1);
  not not_6 (not_6_out, or_5_out);
  and and_8 (and_8_out, 1'b1, 1'b1, or_5_out);
  and and_9 (and_9_out, not_4_out, not_5_out, or_5_out);
  and and_10 (and_10_out, not_4_out, 1'b1, not_6_out);
  and and_11 (and_11_out, 1'b1, not_5_out, not_6_out);
  and and_12 (and_12_out, 1'b1, 1'b1);
  and and_13 (and_13_out, 1'b1, or_5_out);
  and and_14 (and_14_out, or_5_out, 1'b1);
  or or_3 (or_3_out, and_12_out, and_13_out, and_14_out);
  or or_4 (or_8_out[2], and_8_out, and_9_out, and_10_out, and_11_out);
  // Probe on or_8_out
  not not_7 (not_7_out, 1'b1);
  not not_8 (not_8_out, 1'b0);
  not not_9 (not_9_out, or_7_out);
  and and_15 (and_15_out, 1'b1, 1'b0, or_7_out);
  and and_16 (and_16_out, not_7_out, not_8_out, or_7_out);
  and and_17 (and_17_out, not_7_out, 1'b0, not_9_out);
  and and_18 (and_18_out, 1'b1, not_9_out);
  and and_19 (and_19_out, 1'b1, 1'b0);
  and and_20 (and_20_out, 1'b0, or_7_out);
  and and_21 (and_21_out, or_7_out, 1'b1);
  or or_5 (or_5_out, and_19_out, and_20_out, and_21_out);
  or or_6 (or_8_out[1], and_15_out, and_16_out, and_17_out, and_18_out);
  Clock clock_1 (.out(clock_1_out));
  not not_10 (not_10_out, clock_1_out);
  not not_11 (not_11_out, 1'b1);
  not not_12 (not_12_out, 1'b0);
  and and_22 (and_22_out, clock_1_out, 1'b1, 1'b0);
  and and_23 (and_23_out, not_10_out, not_11_out, 1'b0);
  and and_24 (and_24_out, not_10_out, 1'b1, not_12_out);
  and and_25 (and_25_out, clock_1_out, not_11_out, not_12_out);
  and and_26 (and_26_out, clock_1_out, 1'b1);
  and and_27 (and_27_out, 1'b1, 1'b0);
  and and_28 (and_28_out, 1'b0, clock_1_out);
  or or_7 (or_7_out, and_26_out, and_27_out, and_28_out);
  or or_8 (or_8_out[0], and_22_out, and_23_out, and_24_out, and_25_out);
endmodule
